# Fritzing sketch PCB (saved by Fritzing 0.9.3b)
circuit board: 9.2cm x 6.8cm
breadboards: 1

parts:
  teensy_napajanje = female pin header, 14 pins [form="♀ (female)"]
  R_led = Resistor [tolerance=±5% resistance=220 package=THT]
  R_start = Resistor [tolerance=±5% resistance=10k package=THT]
  J2 = female pin header, 1 pin [form="♀ (female)"]
  R_zaslon = Resistor [tolerance=±5% resistance=220 package=THT]
  vhod2 = female pin header, 1 pin [form="♀ (female)"]
  J4 = female pin header, 5 pins [form="♀ (female)"]
  LCD1 = LCD screen
  R1 = TRIMPOT [package=trim_pot_pth]
  LED2 = LED - 5mm [color="Red (633nm)" package="5 mm [THT]"]
  S2 = Pushbutton [package="[THT]"]
  S1 = Pushbutton [package="[THT]"]
  R2 = Resistor [tolerance=±5% resistance=10k package=THT]
  teensy_gnd = female pin header, 6 pins [form="♀ (female)"]
  J8 = female pin header, 5 pins [form="♀ (female)"]
  J9 = female pin header, 8 pins [form="♀ (female)"]
  J10 = female pin header, 8 pins [form="♀ (female)"]
  J15 = female pin header, 1 pin [form="♀ (female)"]
  J16 = female pin header, 1 pin [form="♀ (female)"]
  J17 = female pin header, 2 pins [form="♀ (female)"]  # not connected
  J18 = female pin header, 2 pins [form="♀ (female)"]

nets:
  N1: teensy_napajanje.pin1, J4.pin4
  N2: teensy_napajanje.pin3, J18.pin2
  N3: teensy_napajanje.pin6, LCD1.DB7
  N4: teensy_napajanje.pin7, LCD1.DB6
  N5: teensy_napajanje.pin8, LCD1.DB5
  N6: teensy_napajanje.pin9, LCD1.DB4
  N7: teensy_napajanje.pin10, LCD1.E
  N8: teensy_napajanje.pin11, LCD1.RS
  N9: teensy_napajanje.pin12, J4.pin1, S1.Pin_3, R2.Pin_0, J18.pin1
  N10: teensy_napajanje.pin14, R_zaslon.Pin_0, LCD1.VDD, R1.CW, J10.pin8, J16.pin1
  N11: R_led.Pin_0, LED2.cathode
  N12: R_led.Pin_1, J9.pin4
  N13: R_start.Pin_0, J2.pin1, vhod2.pin1, LCD1.VSS, LCD1.R/W, LCD1.LED-, S2.Pin_1, S2.Pin_2, J10.pin7, J15.pin1
  N14: R_start.Pin_1, S1.Pin_1, S1.Pin_2, teensy_gnd.pin3
  N15: R_zaslon.Pin_1, LCD1.LED+
  N16: J4.pin2, J8.pin3
  N17: J4.pin3, J8.pin4
  N18: J4.pin5, J8.pin5
  N19: LCD1.V0, R1.WIPER
  N20: S2.Pin_3, S2.Pin_4, R2.Pin_1
  N21: teensy_gnd.pin1, J10.pin1
  N22: teensy_gnd.pin2, J10.pin2
