# Fritzing sketch Shema merilnika (saved by Fritzing 0.9.3b)
breadboards: 1

parts:
  WeMos_D1_Mini1 = WeMos D1 Mini
  Teensy_3_1 = Teensy 3.1  # not connected
  U1 = LCD-16X2 [package=lcd-16x2]
  microSD_Transflash1 = SparkFun - microSD Transflash
  U2 = POT [package=pot_alpha_rv16af-20]
  R1 = Resistor [tolerance=±5% resistance=220 package="1206 [SMD]"]
  S1 = Pushbutton [package="[THT]"]
  S2 = Pushbutton [package="[THT]"]
  R2 = Resistor [tolerance=±5% resistance=10k package="1206 [SMD]"]
  R3 = Resistor [tolerance=±5% resistance=10k package="1206 [SMD]"]
  Part1 = Triple Axis Accelerometer Breakout - ADXL335

nets:
  N1: WeMos_D1_Mini1.5V, U2.E, R1.Pin_0, S1.Pin_3, S1.Pin_4
  GND: WeMos_D1_Mini1.G, U1.R_W, microSD_Transflash1.GND, U2.A, S2.Pin_1, S2.Pin_2, R3.Pin_0, Part1.GND
  N2: WeMos_D1_Mini1.RST, S2.Pin_3, S2.Pin_4, R2.Pin_0
  N3: U1.VO, U2.S
  VCC: microSD_Transflash1.VCC, R2.Pin_1, Part1.VCC
  N4: S1.Pin_1, S1.Pin_2, R3.Pin_1

custom parts:
  WeMos D1 Mini: The D1 mini is a mini wifi board based on ESP-8266EX.
